# Fritzing sketch CySump (saved by Fritzing 0.9.3b)
circuit board: 12.2109cm x 9.21139cm
breadboards: 2

parts:
  Power_Relay_Featherwing = Adafruit PowerRelay Feather Wing [part_number="Adafruit #3191"]
  LED2 = LED - 5mm [color="Red (633nm)" package="5 mm [THT]"]
  LED1 = LED - 5mm [color="Green (570nm)" package="5 mm [THT]"]
  LED3 = LED - 5mm [color="Yellow (595nm)" package="5 mm [THT]"]
  J1 = Piezo Speaker
  J2 = Screw terminal - 2 pins [package=THT]
  HC-SR04_Sensor_(or_JSN-SR04T) = HC-SR04 Ultrasonic Distance Sensor
  S1 = SPST Switch [package=switche-dpdt]
  Huzzah_ESP8266 = Adafruit HUZZAH ESP8266 [part_number="Adafruit #2471"]

nets:
  3.3V: Power_Relay_Featherwing.3.3V, Huzzah_ESP8266.3.3V
  GND: Power_Relay_Featherwing.GND, LED2.cathode, LED1.cathode, LED3.cathode, J1.pin1, J2.pin1, HC-SR04_Sensor_(or_JSN-SR04T).GND, Huzzah_ESP8266.GND
  N1: Power_Relay_Featherwing.A, Huzzah_ESP8266.GPIO15
  N2: LED2.anode, Huzzah_ESP8266.GPIO4
  N3: LED1.anode, Huzzah_ESP8266.GPIO2
  N4: LED3.anode, Huzzah_ESP8266.GPIO5
  N5: J1.pin2, Huzzah_ESP8266.GPIO16
  N6: J2.pin2, HC-SR04_Sensor_(or_JSN-SR04T).VCC, S1.P
  N7: HC-SR04_Sensor_(or_JSN-SR04T).TRIG, Huzzah_ESP8266.GPIO12
  N8: HC-SR04_Sensor_(or_JSN-SR04T).ECHO, Huzzah_ESP8266.GPIO14
  N9: S1.O, Huzzah_ESP8266.VIN

notes:
  CySump Board Rev 1.2
  WiFi Act
  Alarm
  Pump
  Note: HC-SR04 Schematic is incorrect.  GND and ECHO pins are swapped.
  -
  +
  5V DC 0.5A
  VCC of HC-SR04 intentionally wired to 5V instead of 3.3V because it is intended to be replaced by JSN-SR04T which is waterproof.
  (c) 2019 Cyrus Brunner
  www.cyrusbuilt.net
  Piezo
  PWR
  CySump Controller, Automated IoT Sump Pump Controller, 1.2
  FAB 00100 ASSY 00102
  Sonar-Activated IoT Sump Pump Controller

custom parts:
  Adafruit PowerRelay Feather Wing: A Feather board without ambition is a Feather board without FeatherWings! This is the Power Relay FeatherWing. It gives you power to control, and control over power. Put simply, you can now turn on and off lamps, fans, solenoids, and other small appliances that run on up to 250VAC or DC power using any Feather board. Compared to our smaller Relay FeatherWings, this one can handle a beefy 1200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
  Adafruit HUZZAH ESP8266: Add Internet to your next project with an adorable, bite-sized WiFi microcontroller, at a price you like! The ESP8266 processor from Espressif is an 80 MHz microcontroller with a full WiFi front-end (both as client and access point) and TCP/IP stack with DNS support as well. While this chip has been very popular, its also been very difficult to use. Most of the low cost modules are not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
